// Logisim project jaide.circ as structural Verilog: 1 circuit, main circuit main
module main (
);

  wire clk_out;
  wire [15:0] pc_q, rom_1_data;

  Button clk (.out(clk_out));
  Register #(.width(16)) pc (.clk(clk_out), .Q(pc_q));  // open: D, en, clr
  ROM #(.addrWidth(16), .dataWidth(16)) rom_1 (.addr(pc_q), .data(rom_1_data));
endmodule
